# Fritzing sketch Hardware (saved by Fritzing 0.9.9b)
breadboards: 1

parts:
  Raspberry_Pi_1 = Raspberry Pi 3 [part_number=RPI-3-V1.2]
  J1 = Basic Servo
  CAMERA1 = TTL_Serial_JPEG_Camera  # not connected
  DRV_1 = DRV 8825 Stepper Motor Carrier, High Current [part_number="DRV 8825"]
  Power_plug1 = Power plug
  M3 = Stepper Motor - Bipolar  # not connected
  DRV_2 = DRV 8825 Stepper Motor Carrier, High Current [part_number="DRV 8825"]
  M4 = Stepper Motor - Bipolar  # not connected
  Componente1 = Arduino Uno (Rev3)

nets:
  N1: Raspberry_Pi_1.GIPO14, J1.pulse
  GND: Raspberry_Pi_1.GND, J1.gnd
  5V: Raspberry_Pi_1.5V, J1.vcc
  N2: DRV_1.STEP, Componente1.D9_PWM
  N3: DRV_1.DIRECTION, Componente1.D10_PWM/SS
  N4: DRV_1.VOLTAGE_DD, DRV_2.VOLTAGE_DD, Componente1.5V
  N5: DRV_1.GROUND_LOG, DRV_2.GROUND_LOG, Componente1.GND
  N6: Power_plug1.GND, DRV_2.VOLTAGE_ST/_MT
  N7: Power_plug1.VCC, DRV_2.GROUND_ST/_MT
